// Digital circuit 1-1 REGISTER.dig as structural Verilog
module _1_1_REGISTER (
  input  Data_in,
  input  Sel,
  input  Clk,
  output Data_out
);

  wire multiplexer_1_out;

  Multiplexer multiplexer_1 (.sel(Sel), .in_0(Data_out), .in_1(Data_in), .out(multiplexer_1_out));
  D_FF d_ff_1 (.D(multiplexer_1_out), .C(Clk), .Q(Data_out));  // open: nQ

  // Other names for the same wires on the sheet: D = Data_in; dout = Data_out; S = Sel
endmodule
