// Digital circuit 1-1 SRAM.dig as structural Verilog
module _1_1_SRAM (
  input  Read_D1,
  input  Data_in,
  input  Sel,
  input  Clk,
  output Data_out
);

  wire multiplexer_1_out, Q;

  Multiplexer multiplexer_1 (.sel(Sel), .in_0(Q), .in_1(Data_in), .out(multiplexer_1_out));
  D_FF d_ff_1 (.D(multiplexer_1_out), .C(Clk), .Q(Q));  // open: nQ
  and and_1 (Data_out, Read_D1, Q);

  // Other names for the same wires on the sheet: D = Data_in; RD1 = Read_D1; S = Sel
endmodule
