// Digital circuit 1-15 SRAM.dig as structural Verilog
module _1_15_SRAM (
  input  R_Data1,
  input  [14:0] W_Data,
  input  WS,
  input  clk,
  output [14:0] R_Data
);

  _1_1_SRAM _1_1_sram_1 (.Read_D1(R_Data1), .Data_in(W_Data[0]), .Sel(WS), .Clk(clk), .Data_out(R_Data[0]));
  _1_1_SRAM _1_1_sram_2 (.Read_D1(R_Data1), .Data_in(W_Data[1]), .Sel(WS), .Clk(clk), .Data_out(R_Data[1]));
  _1_1_SRAM _1_1_sram_3 (.Read_D1(R_Data1), .Data_in(W_Data[2]), .Sel(WS), .Clk(clk), .Data_out(R_Data[2]));
  _1_1_SRAM _1_1_sram_4 (.Read_D1(R_Data1), .Data_in(W_Data[3]), .Sel(WS), .Clk(clk), .Data_out(R_Data[3]));
  _1_1_SRAM _1_1_sram_5 (.Read_D1(R_Data1), .Data_in(W_Data[4]), .Sel(WS), .Clk(clk), .Data_out(R_Data[4]));
  _1_1_SRAM _1_1_sram_6 (.Read_D1(R_Data1), .Data_in(W_Data[5]), .Sel(WS), .Clk(clk), .Data_out(R_Data[5]));
  _1_1_SRAM _1_1_sram_7 (.Read_D1(R_Data1), .Data_in(W_Data[6]), .Sel(WS), .Clk(clk), .Data_out(R_Data[6]));
  _1_1_SRAM _1_1_sram_8 (.Read_D1(R_Data1), .Data_in(W_Data[7]), .Sel(WS), .Clk(clk), .Data_out(R_Data[7]));
  _1_1_SRAM _1_1_sram_9 (.Read_D1(R_Data1), .Data_in(W_Data[8]), .Sel(WS), .Clk(clk), .Data_out(R_Data[8]));
  _1_1_SRAM _1_1_sram_10 (.Read_D1(R_Data1), .Data_in(W_Data[9]), .Sel(WS), .Clk(clk), .Data_out(R_Data[9]));
  _1_1_SRAM _1_1_sram_11 (.Read_D1(R_Data1), .Data_in(W_Data[10]), .Sel(WS), .Clk(clk), .Data_out(R_Data[10]));
  _1_1_SRAM _1_1_sram_12 (.Read_D1(R_Data1), .Data_in(W_Data[11]), .Sel(WS), .Clk(clk), .Data_out(R_Data[11]));
  _1_1_SRAM _1_1_sram_13 (.Read_D1(R_Data1), .Data_in(W_Data[12]), .Sel(WS), .Clk(clk), .Data_out(R_Data[12]));
  _1_1_SRAM _1_1_sram_14 (.Read_D1(R_Data1), .Data_in(W_Data[13]), .Sel(WS), .Clk(clk), .Data_out(R_Data[13]));
  _1_1_SRAM _1_1_sram_15 (.Read_D1(R_Data1), .Data_in(W_Data[14]), .Sel(WS), .Clk(clk), .Data_out(R_Data[14]));

  // Other names for the same wires on the sheet: d0 = R_Data[0]; d1 = R_Data[1]; d2 = R_Data[2]; d3 = R_Data[3];
  //   d4 = R_Data[4]; d5 = R_Data[5]; d6 = R_Data[6]; d7 = R_Data[7]; d8 = R_Data[8]; d9 = R_Data[9];
  //   d10 = R_Data[10]; d11 = R_Data[11]; d12 = R_Data[12]; d13 = R_Data[13]; d14 = R_Data[14]; RD1 = R_Data1;
  //   SEL = WS; WD0 = W_Data[0]; WD1 = W_Data[1]; WD2 = W_Data[2]; WD3 = W_Data[3]; WD4 = W_Data[4]; WD5 = W_Data[5];
  //   WD6 = W_Data[6]; WD7 = W_Data[7]; WD8 = W_Data[8]; WD9 = W_Data[9]; WD10 = W_Data[10]; WD11 = W_Data[11];
  //   WD12 = W_Data[12]; WD13 = W_Data[13]; wd14 = W_Data[14]
endmodule
