// Digital circuit 1-6 REGISTER.dig as structural Verilog
module _1_6_REGISTER (
  input  [5:0] Data_in,
  input  Sel,
  input  Clk,
  output [5:0] Data_out
);

  _1_1_REGISTER _1_1_register_1 (.Data_in(Data_in[0]), .Sel(Sel), .Clk(Clk), .Data_out(Data_out[0]));
  _1_1_REGISTER _1_1_register_2 (.Data_in(Data_in[1]), .Sel(Sel), .Clk(Clk), .Data_out(Data_out[1]));
  _1_1_REGISTER _1_1_register_3 (.Data_in(Data_in[2]), .Sel(Sel), .Clk(Clk), .Data_out(Data_out[2]));
  _1_1_REGISTER _1_1_register_4 (.Data_in(Data_in[3]), .Sel(Sel), .Clk(Clk), .Data_out(Data_out[3]));
  _1_1_REGISTER _1_1_register_5 (.Data_in(Data_in[4]), .Sel(Sel), .Clk(Clk), .Data_out(Data_out[4]));
  _1_1_REGISTER _1_1_register_6 (.Data_in(Data_in[5]), .Sel(Sel), .Clk(Clk), .Data_out(Data_out[5]));

  // Other names for the same wires on the sheet: d0 = Data_in[0]; d1 = Data_in[1]; d2 = Data_in[2]; d3 = Data_in[3];
  //   d4 = Data_in[4]; d5 = Data_in[5]; do0 = Data_out[0]; do1 = Data_out[1]; do2 = Data_out[2]; do3 = Data_out[3];
  //   do4 = Data_out[4]; do5 = Data_out[5]; s = Sel
endmodule
