// Digital circuit 3- BIT COUNTER.dig as structural Verilog
module _3__BIT_COUNTER (
  input  [2:0] D_in,
  input  Clk,
  output [2:0] D_out
);

  _1_1_REGISTER _1_1_register_1 (.Data_in(D_in[0]), .Sel(1'b1), .Clk(Clk), .Data_out(D_out[0]));
  _1_1_REGISTER _1_1_register_2 (.Data_in(D_in[1]), .Sel(1'b1), .Clk(Clk), .Data_out(D_out[1]));
  _1_1_REGISTER _1_1_register_3 (.Data_in(D_in[2]), .Sel(1'b1), .Clk(Clk), .Data_out(D_out[2]));

  // Other names for the same wires on the sheet: D00 = D_out[0]; D0 = D_in[0]; D1 = D_in[1]; D2 = D_in[2];
  //   DO1 = D_out[1]; DO2 = D_out[2]
endmodule
