// Digital circuit 6-6 REGISTER SET.dig as structural Verilog
module _6_6_REGISTER_SET (
  input  Clk,
  input  [5:0] WD,
  input  [2:0] WA,
  input  RWE,
  input  [2:0] RA,
  input  [2:0] RB,
  output [5:0] RData_1,
  output [5:0] RData_2
);

  wire and_1_out, and_2_out, and_3_out, and_4_out, and_5_out, and_6_out, s0, s1, s2, s3, s4, s5;
  wire [5:0] D0, D1, D2, D3, D4, D5;

  Decoder #(.Selector_Bits(3)) decoder_1 (
    .sel(WA), .out_0(s0), .out_1(s1), .out_2(s2), .out_3(s3), .out_4(s4), .out_5(s5));  // open: out_6, out_7
  and and_1 (and_1_out, RWE, s0);
  and and_2 (and_2_out, RWE, s1);
  and and_3 (and_3_out, RWE, s2);
  and and_4 (and_4_out, RWE, s3);
  and and_5 (and_5_out, RWE, s4);
  and and_6 (and_6_out, RWE, s5);
  _1_6_REGISTER _1_6_register_1 (.Data_in(WD), .Sel(and_1_out), .Clk(Clk), .Data_out(D0));
  _1_6_REGISTER _1_6_register_2 (.Data_in(WD), .Sel(and_2_out), .Clk(Clk), .Data_out(D1));
  _1_6_REGISTER _1_6_register_3 (.Data_in(WD), .Sel(and_3_out), .Clk(Clk), .Data_out(D2));
  _1_6_REGISTER _1_6_register_4 (.Data_in(WD), .Sel(and_4_out), .Clk(Clk), .Data_out(D3));
  _1_6_REGISTER _1_6_register_5 (.Data_in(WD), .Sel(and_5_out), .Clk(Clk), .Data_out(D4));
  _1_6_REGISTER _1_6_register_6 (.Data_in(WD), .Sel(and_6_out), .Clk(Clk), .Data_out(D5));
  Multiplexer #(.Selector_Bits(3), .Bits(6)) multiplexer_1 (
    .sel(RA), .in_0(D0), .in_1(D1), .in_2(D2), .in_3(D3), .in_4(D4), .in_5(D5), .in_6({6{1'b0}}),
    .in_7({6{1'b0}}), .out(RData_1));
  Multiplexer #(.Selector_Bits(3), .Bits(6)) multiplexer_2 (
    .sel(RB), .in_0(D0), .in_1(D1), .in_2(D2), .in_3(D3), .in_4(D4), .in_5(D5), .in_6({6{1'b0}}),
    .in_7({6{1'b0}}), .out(RData_2));

  // Other names for the same wires on the sheet: Din[5:0] = WD
endmodule
