// Digital circuit 6-BIT ADDER.dig as structural Verilog
module _6_BIT_ADDER (
  input  [5:0] B,
  input  [5:0] A,
  output [5:0] Sum,
  output C_out
);

  wire fa_1_c_out, fa_2_c_out, fa_3_c_out, fa_4_c_out, fa_5_c_out;

  FA fa_1 (.A(A[0]), .B(B[0]), .C_in(1'b0), .Sum(Sum[0]), .C_out(fa_1_c_out));
  FA fa_2 (.A(A[1]), .B(B[1]), .C_in(fa_1_c_out), .Sum(Sum[1]), .C_out(fa_2_c_out));
  FA fa_3 (.A(A[2]), .B(B[2]), .C_in(fa_2_c_out), .Sum(Sum[2]), .C_out(fa_3_c_out));
  FA fa_4 (.A(A[3]), .B(B[3]), .C_in(fa_3_c_out), .Sum(Sum[3]), .C_out(fa_4_c_out));
  FA fa_5 (.A(A[4]), .B(B[4]), .C_in(fa_4_c_out), .Sum(Sum[4]), .C_out(fa_5_c_out));
  FA fa_6 (.A(A[5]), .B(B[5]), .C_in(fa_5_c_out), .Sum(Sum[5]), .C_out(C_out));

  // Other names for the same wires on the sheet: s0 = Sum[0]; s1 = Sum[1]; s2 = Sum[2]; s3 = Sum[3]; s4 = Sum[4];
  //   s5 = Sum[5]
endmodule
