// Digital circuit 6-BIT ALU.dig as structural Verilog
module _6_BIT_ALU (
  input  [5:0] A,
  input  [5:0] B,
  input  [1:0] OPC,
  output [5:0] Output,
  output ZF,
  output SF
);

  wire or_1_out;
  wire [5:0] _6_bit_adder_1_sum, _6_bit_shr_1_output, _6_bit_xor_1_xor;

  _6_BIT_ADDER _6_bit_adder_1 (.A(A), .B(B), .Sum(_6_bit_adder_1_sum));  // open: C_out
  _6_bit_XOR _6_bit_xor_1 (.A(A), .B(B), .Xor(_6_bit_xor_1_xor));
  _6_bit_SHR _6_bit_shr_1 (.A(A), .Shr(B[2:0]), .Output(_6_bit_shr_1_output));
  Multiplexer #(.Selector_Bits(2), .Bits(6)) multiplexer_1 (
    .sel(OPC), .in_0(_6_bit_adder_1_sum), .in_1(_6_bit_xor_1_xor), .in_2(_6_bit_shr_1_output),
    .in_3({6{1'b0}}), .out(Output));
  or or_1 (or_1_out, Output[0], Output[1], Output[2], Output[3], Output[4], Output[5]);
  not not_1 (ZF, or_1_out);

  assign SF = Output[5];
endmodule
