// Digital circuit 6-BIT CPU.dig as structural Verilog
module _6_BIT_CPU (
  input  [14:0] ISA,
  input  Cpu_Clk,
  output [2:0] RA1
);

  wire IMM_SEL, JMp_Sel, SF, WR_en, ZF;
  wire [1:0] OPC;
  wire [2:0] multiplexer_1_out, NX_ADD;
  wire [5:0] A, ANS, B, RD2;

  Multiplexer #(.Bits(3)) multiplexer_1 (.sel(JMp_Sel), .in_0(NX_ADD), .in_1(ISA[11:9]), .out(multiplexer_1_out));
  _3__BIT_COUNTER _3__bit_counter_1 (.D_in(multiplexer_1_out), .Clk(Cpu_Clk), .D_out(RA1));
  PLUS_1 plus_1_1 (.Din(RA1), .Dout(NX_ADD));
  controll_unit controll_unit_1 (
    .OPC_IN(ISA[14:11]), .ZF(ZF), .SF(SF), .OPC(OPC), .Imm_SEL(IMM_SEL), .WRE(WR_en), .JMP_SEL(JMp_Sel));
  _6_6_REGISTER_SET _6_6_register_set_1 (
    .Clk(Cpu_Clk), .WD(ANS), .WA(ISA[10:8]), .RWE(WR_en), .RA(ISA[10:8]), .RB(ISA[7:5]), .RData_1(A),
    .RData_2(RD2));
  _6_BIT_ALU _6_bit_alu_1 (.A(A), .B(B), .OPC(OPC), .Output(ANS), .ZF(ZF), .SF(SF));
  Multiplexer #(.Bits(6)) multiplexer_2 (.sel(IMM_SEL), .in_0(RD2), .in_1(ISA[7:2]), .out(B));

  // Other names for the same wires on the sheet: a12 = ISA[2]; a11 = ISA[3]; a10 = ISA[4]; a9 = ISA[5];
  //   RB[2:0] = ISA[7:5]; a8 = ISA[6]; a7 = ISA[7]; a6 = ISA[8]; RA[2:0] = ISA[10:8]; a5 = ISA[9];
  //   J_ADD[2:0] = ISA[11:9]; a4 = ISA[10]; a3 = ISA[11]; a2 = ISA[12]; a1 = ISA[13]; a0 = ISA[14]; R_ADD[2:0] = RA1
endmodule
