// Digital circuit 6-bit SHR.dig as structural Verilog
module _6_bit_SHR (
  input  [5:0] A,
  input  [2:0] Shr,
  output [5:0] Output
);

  Multiplexer #(.Selector_Bits(3)) multiplexer_1 (
    .sel(Shr), .in_0(A[5]), .in_1(1'b0), .in_2(1'b0), .in_3(1'b0), .in_4(1'b0), .in_5(1'b0), .in_6(1'b0),
    .in_7(1'b0), .out(Output[5]));
  Multiplexer #(.Selector_Bits(3)) multiplexer_2 (
    .sel(Shr), .in_0(A[4]), .in_1(A[5]), .in_2(1'b0), .in_3(1'b0), .in_4(1'b0), .in_5(1'b0), .in_6(1'b0),
    .in_7(1'b0), .out(Output[4]));
  Multiplexer #(.Selector_Bits(3)) multiplexer_3 (
    .sel(Shr), .in_0(A[3]), .in_1(A[4]), .in_2(A[5]), .in_3(1'b0), .in_4(1'b0), .in_5(1'b0), .in_6(1'b0),
    .in_7(1'b0), .out(Output[3]));
  Multiplexer #(.Selector_Bits(3)) multiplexer_4 (
    .sel(Shr), .in_0(A[2]), .in_1(A[3]), .in_2(A[4]), .in_3(A[5]), .in_4(1'b0), .in_5(1'b0), .in_6(1'b0),
    .in_7(1'b0), .out(Output[2]));
  Multiplexer #(.Selector_Bits(3)) multiplexer_5 (
    .sel(Shr), .in_0(A[1]), .in_1(A[2]), .in_2(A[3]), .in_3(A[4]), .in_4(A[5]), .in_5(1'b0), .in_6(1'b0),
    .in_7(1'b0), .out(Output[1]));
  Multiplexer #(.Selector_Bits(3)) multiplexer_6 (
    .sel(Shr), .in_0(A[0]), .in_1(A[1]), .in_2(A[2]), .in_3(A[3]), .in_4(A[4]), .in_5(A[5]), .in_6(1'b0),
    .in_7(1'b0), .out(Output[0]));

  // Other names for the same wires on the sheet: s0 = Output[0]; s1 = Output[1]; s2 = Output[2]; s3 = Output[3];
  //   s4 = Output[4]; s5 = Output[5]
endmodule
