// Digital circuit 6-bit XOR.dig as structural Verilog
module _6_bit_XOR (
  input  [5:0] A,
  input  [5:0] B,
  output [5:0] Xor
);

  xor xor_1 (Xor[0], A[0], B[0]);
  xor xor_2 (Xor[1], A[1], B[1]);
  xor xor_3 (Xor[2], A[2], B[2]);
  xor xor_4 (Xor[3], A[3], B[3]);
  xor xor_5 (Xor[4], A[4], B[4]);
  xor xor_6 (Xor[5], A[5], B[5]);

  // Other names for the same wires on the sheet: s0 = Xor[0]; s1 = Xor[1]; s2 = Xor[2]; s3 = Xor[3]; s4 = Xor[4];
  //   s5 = Xor[5]
endmodule
