// Digital circuit 7-15 SRAM.dig as structural Verilog
module _7_15_SRAM (
  input  clk,
  input  [14:0] W_data,
  input  RAM_en,
  input  [2:0] WS,
  input  [2:0] RDS,
  output [14:0] Data_out
);

  wire and_1_out, and_2_out, and_3_out, and_4_out, and_5_out, and_6_out, and_7_out, RDS0, RDS1, RDS2, RDS3,
       RDS4, RDS5, RDS6, WS0, WS1, WS2, WS3, WS4, WS5, WS6;
  wire [14:0] RD0, RD1, RD2, RD3, RD4, RD5, RD6;

  Decoder #(.Selector_Bits(3)) decoder_1 (
    .sel(WS), .out_0(WS0), .out_1(WS1), .out_2(WS2), .out_3(WS3), .out_4(WS4), .out_5(WS5), .out_6(WS6));  // open: out_7
  Decoder #(.Selector_Bits(3)) decoder_2 (
    .sel(RDS), .out_0(RDS0), .out_1(RDS1), .out_2(RDS2), .out_3(RDS3), .out_4(RDS4), .out_5(RDS5),
    .out_6(RDS6));  // open: out_7
  and and_1 (and_1_out, WS0, RAM_en);
  and and_2 (and_2_out, WS1, RAM_en);
  and and_3 (and_3_out, WS2, RAM_en);
  and and_4 (and_4_out, WS3, RAM_en);
  and and_5 (and_5_out, WS4, RAM_en);
  and and_6 (and_6_out, WS5, RAM_en);
  and and_7 (and_7_out, WS6, RAM_en);
  _1_15_SRAM _1_15_sram_1 (.R_Data1(RDS0), .W_Data(W_data), .WS(and_1_out), .clk(clk), .R_Data(RD0));
  _1_15_SRAM _1_15_sram_2 (.R_Data1(RDS1), .W_Data(W_data), .WS(and_2_out), .clk(clk), .R_Data(RD1));
  _1_15_SRAM _1_15_sram_3 (.R_Data1(RDS2), .W_Data(W_data), .WS(and_3_out), .clk(clk), .R_Data(RD2));
  _1_15_SRAM _1_15_sram_4 (.R_Data1(RDS3), .W_Data(W_data), .WS(and_4_out), .clk(clk), .R_Data(RD3));
  _1_15_SRAM _1_15_sram_5 (.R_Data1(RDS4), .W_Data(W_data), .WS(and_5_out), .clk(clk), .R_Data(RD4));
  _1_15_SRAM _1_15_sram_6 (.R_Data1(RDS5), .W_Data(W_data), .WS(and_6_out), .clk(clk), .R_Data(RD5));
  _1_15_SRAM _1_15_sram_7 (.R_Data1(RDS6), .W_Data(W_data), .WS(and_7_out), .clk(clk), .R_Data(RD6));
  assign Data_out = RD0 | RD1 | RD2 | RD3 | RD4 | RD5 | RD6;  // Or or_1, 15 bits wide

  // Other names for the same wires on the sheet: en = RAM_en; WD[14:0] = W_data
endmodule
