// Digital circuit FA.dig as structural Verilog
module FA (
  input  B,
  input  C_in,
  input  A,
  output Sum,
  output C_out
);

  wire ha_1_c_out, ha_1_sum, ha_2_c_out;

  HA ha_1 (.A(A), .B(B), .Sum(ha_1_sum), .C_out(ha_1_c_out));
  HA ha_2 (.A(ha_1_sum), .B(C_in), .Sum(Sum), .C_out(ha_2_c_out));
  or or_1 (C_out, ha_2_c_out, ha_1_c_out);
endmodule
