// Digital circuit PLUS 1.dig as structural Verilog
module PLUS_1 (
  input  [2:0] Din,
  output [2:0] Dout
);

  Add #(.Bits(3)) add_1 (.a(Din), .b(3'b001), .c_i(1'b0), .s(Dout));  // open: c_o
endmodule
