// Digital circuit controll unit.dig as structural Verilog
module controll_unit (
  input  [3:0] OPC_IN,
  input  ZF,
  input  SF,
  output [1:0] OPC,
  output Imm_SEL,
  output WRE,
  output JMP_SEL
);

  wire and_1_out, and_3_out, and_4_out, not_1_out, not_2_out, not_3_out, not_4_out, not_5_out, not_6_out,
       not_7_out, or_1_out;

  not not_1 (not_1_out, ZF);
  not not_2 (not_2_out, SF);
  and and_1 (and_1_out, OPC_IN[1], not_1_out, not_2_out);
  not not_3 (not_3_out, OPC_IN[3]);
  not not_4 (not_4_out, OPC_IN[3]);
  not not_5 (not_5_out, OPC_IN[2]);
  or or_1 (or_1_out, not_6_out, and_1_out);
  not not_6 (not_6_out, OPC_IN[1]);
  and and_2 (Imm_SEL, not_3_out, OPC_IN[2]);
  and and_3 (and_3_out, not_4_out, not_5_out);
  not not_7 (not_7_out, OPC_IN[2]);
  and and_4 (and_4_out, not_7_out, OPC_IN[3]);
  and and_5 (JMP_SEL, or_1_out, and_4_out);
  or or_2 (WRE, Imm_SEL, and_3_out);

  assign OPC = OPC_IN[1:0];

  // Other names for the same wires on the sheet: OP3 = OPC_IN[0]; OP2 = OPC_IN[1]; OP1 = OPC_IN[2]; OP0 = OPC_IN[3]
endmodule
